# Fritzing sketch Untitled Sketch (saved by Fritzing 1.0.6)
breadboards: 2

parts:
  A1 = Esp32-c3 super mini
  A2 = Esp32-c3 super mini
  Composant1 = Adafruit Thermocouple Amplifier MAX31855 [part_number="Adafruit #269"]  # not connected
  Display1 = 4-Digit 7-segment LED Display [package=THT]  # not connected
  Display2 = 4-Digit 7-segment LED Display [package=THT]  # not connected
  Display3 = 4-Digit 7-segment LED Display [package=THT]  # not connected
  Display4 = 4-Digit 7-segment LED Display [package=THT]  # not connected
  12_V = male pin header, 2 pins [form="♂ (male)"]
  I²C = male pin header, 2 pins [form="♂ (male)"]  # not connected
  5V = male pin header, 2 pins [form="♂ (male)"]  # not connected
  J3 = female pin header, 7 pins [form="♀ (female)"]
  J4 = male pin header, 7 pins [form="♂ (male)"]  # not connected
  1_-_10 = male pin header, 10 pins [form="♂ (male)"]
  J5 = male pin header, 10 pins [form="♂ (male)"]
  AFR = female pin header, 2 pins [form="♀ (female)"]  # not connected
  BAT2 = Battery Holders [package=battcon_12mm]
  Adafruit#1 = Adafruit ADS1115 16-Bit ADC [part_number=1085]  # not connected
  Composant2 = Adafruit Thermocouple Amplifier MAX31855 [part_number="Adafruit #269"]  # not connected

nets:
  N1: A1.Pin_4, 1_-_10.pin4
  N2: A1.Pin_5, 1_-_10.pin3
  N3: A1.Pin_15, 1_-_10.pin5
  N4: A1.Pin_16, 1_-_10.pin2
  N5: A2.Pin_4, J3.pin4
  N6: A2.Pin_5, J3.pin5
  N7: A2.Pin_15, J3.pin3
  N8: A2.Pin_16, J3.pin6
  N9: 12_V.pin1, J5.pin9, BAT2.+
  N10: 12_V.pin2, J5.pin8, BAT2.-

custom parts:
  Esp32-c3 super mini: ESP32-C3 Development Board ESP32 SuperMini Development Board ESP32 Development Board WiFi Bluetooth.
  Adafruit Thermocouple Amplifier MAX31855: Thermocouples are very sensitive, requiring a good amplifier with a cold-compensation reference. The MAX31855K does everything for you, and can be easily interfaced with any microcontroller, even one without an analog input. This breakout board has the chip itself, a 3.3V regulator with 10uF bypass capacitors and level shifting circuitry, all assembled and tested. Comes with a 2 pin terminal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
  4-Digit 7-segment LED Display: A 4-digit 7-segments LED display PCB module driven by a TM1637 control IC via 1-wire protocol.
  Adafruit ADS1115 16-Bit ADC: For microcontrollers without an analog-to-digital converter or when you want a higher-precision ADC, the ADS1115 provides 16-bit precision at 860 samples/second over I2C. The chip can be configured as 4 single-ended input channels, or two differential channels. As a nice bonus, it even includes a programmable gain amplifier, up to x16, to help boost up smaller single/differential signals to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
