# Fritzing sketch cablage alt (saved by Fritzing 1.0.6)
breadboards: 2

parts:
  A2 = Esp32-c3 super mini
  J3 = female pin header, 7 pins [form="♀ (female)"]
  Composant2 = Adafruit Thermocouple Amplifier MAX31855 [part_number="Adafruit #269"]  # not connected
  Adafruit#2 = Adafruit ADS1115 16-Bit ADC [part_number=1085]
  J6 = female pin header, 5 pins [form="♀ (female)"]
  R1 = Resistor [tolerance=±5% power=0.25W resistance=220 package=THT]
  J7 = female pin header, 7 pins [form="♀ (female)"]
  A3 = Esp32-c3 super mini
  S2 = Taiway 100-SP-X-T1 SPDT Miniature Toggle Switch [part_number=100-SP-X-T1-0-0-B1-M1 package=THT]
  S3 = Taiway 100-SP-X-T1 SPDT Miniature Toggle Switch [part_number=100-SP-X-T1-0-0-B1-M1 package=THT]
  S4 = Taiway 100-SP-X-T1 SPDT Miniature Toggle Switch [part_number=100-SP-X-T1-0-0-B1-M1 package=THT]
  S5 = Taiway 100-SP-X-T1 SPDT Miniature Toggle Switch [part_number=100-SP-X-T1-0-0-B1-M1 package=THT]
  S6 = Taiway 100-SP-X-T1 SPDT Miniature Toggle Switch [part_number=100-SP-X-T1-0-0-B1-M1 package=THT]
  J12 = female pin header, 1 pin [form="♀ (female)"]
  Display5 = 4-Digit 7-segment LED Display [package=THT]  # not connected
  Display6 = 4-Digit 7-segment LED Display [package=THT]  # not connected
  Display7 = 4-Digit 7-segment LED Display [package=THT]  # not connected
  Display8 = 4-Digit 7-segment LED Display [package=THT]  # not connected
  A4 = Mcp23017 Interface Module [package=THT]
  LED1 = LED - 3mm [color="Red (633nm)" current=0.030A package="3 mm [THT]"]  # not connected
  LED2 = LED - 3mm [color="Red (633nm)" current=0.030A package="3 mm [THT]"]  # not connected
  LED3 = LED - 3mm [color="Red (633nm)" current=0.030A package="3 mm [THT]"]  # not connected
  LED4 = LED - 3mm [color="Red (633nm)" current=0.030A package="3 mm [THT]"]  # not connected
  LED5 = LED - 3mm [color="Red (633nm)" current=0.030A package="3 mm [THT]"]  # not connected
  LED6 = LED - 3mm [color="Red (633nm)" current=0.030A package="3 mm [THT]"]  # not connected
  LED7 = LED - 3mm [color="Red (633nm)" current=0.030A package="3 mm [THT]"]  # not connected
  J13 = female pin header, 1 pin [form="♀ (female)"]
  J14 = female pin header, 2 pins [form="♀ (female)"]
  M1 = Niren can bus module [package=THT]
  J16 = female pin header, 1 pin [form="♀ (female)"]
  J17 = female pin header, 1 pin [form="♀ (female)"]
  A5 = Esp32-c3 super mini
  A6 = Mcp23017 Interface Module [package=THT]
  Display9 = 4-Digit 7-segment LED Display [package=THT]
  K1 = Relay [part_number=FRS1B-S package=THT]
  1_-_10_2 = male pin header, 6 pins [form="♂ (male)"]
  1_-_10_3 = male pin header, 6 pins [form="♂ (male)"]
  U1 = Transformer [input_inductance=40H output_inductance=10H input_resistance=1Ω output_resistance=1Ω package=transformer_smd]
  1_-_10_1 = male pin header, 4 pins [form="♂ (male)"]
  U2 = Transformer [input_inductance=40H output_inductance=10H input_resistance=1Ω output_resistance=1Ω package=transformer_smd]

nets:
  N1: A2.Pin_15, J6.pin4, U2.2
  N2: A2.Pin_16, J6.pin5, R1.Pin_0, U2.1
  N3: J3.pin1, K1.COIL1
  N4: J3.pin3, U2.3
  N5: J3.pin6, U2.4
  N6: J3.pin7, Adafruit#2.AIN0
  N7: Adafruit#2.AIN3, J6.pin3
  N8: Adafruit#2.AIN2, J6.pin2
  N9: Adafruit#2.AIN1, J6.pin1
  N10: J7.pin1, S2.L2
  N11: J7.pin7, J13.pin1
  N12: A3.Pin_4, A4.Pin_23, J14.pin2, 1_-_10_1.pin3
  N13: A3.Pin_5, A4.Pin_24, J14.pin1, 1_-_10_1.pin2
  N14: A3.Pin_15, A4.Pin_1, A4.Pin_22, U1.3, 1_-_10_1.pin4
  N15: A3.Pin_16, A4.Pin_11, A4.Pin_21, U1.4, 1_-_10_1.pin1
  N16: S2.L1, S3.L1, S4.L1, S5.L1, S6.L1, J12.pin1
  N17: S3.L2, J16.pin1
  N18: S4.L2, J17.pin1
  N19: M1.pin10, M1.pin12, 1_-_10_2.pin6
  N20: M1.pin11, M1.pin13, 1_-_10_3.pin6
  N21: A5.Pin_4, A6.Pin_24
  N22: A5.Pin_5, A6.Pin_23
  N23: A5.Pin_15, A6.Pin_1, A6.Pin_22, Display9.GND
  N24: A5.Pin_16, A6.Pin_11, A6.Pin_21, Display9.VCC
  N25: A6.Pin_8, Display9.DIO
  N26: A6.Pin_18, Display9.CLK
  N27: 1_-_10_2.pin4, U1.1
  N28: 1_-_10_3.pin1, U1.2

notes:
  AFR
  +12V
  GND
  Power Steering Pump
  +5V
  Air pressure signal
  Air temp signal
  Oil pressure signal
  CONTROL PANEL
  I2C
  FP Relay
  Fan subRelay
  M42 Connector
  1 Can -
  1
  6
  7
  12
  2 ----
  3 IGN
  4 Speed
  5 Injection
  6 Bat +
  11 ----
  12 GND
  10 ill-
  9 ill+
  8 ----
  7 CAN +

custom parts:
  Esp32-c3 super mini: ESP32-C3 Development Board ESP32 SuperMini Development Board ESP32 Development Board WiFi Bluetooth.
  Adafruit Thermocouple Amplifier MAX31855: Thermocouples are very sensitive, requiring a good amplifier with a cold-compensation reference. The MAX31855K does everything for you, and can be easily interfaced with any microcontroller, even one without an analog input. This breakout board has the chip itself, a 3.3V regulator with 10uF bypass capacitors and level shifting circuitry, all assembled and tested. Comes with a 2 pin terminal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
  Adafruit ADS1115 16-Bit ADC: For microcontrollers without an analog-to-digital converter or when you want a higher-precision ADC, the ADS1115 provides 16-bit precision at 860 samples/second over I2C. The chip can be configured as 4 single-ended input channels, or two differential channels. As a nice bonus, it even includes a programmable gain amplifier, up to x16, to help boost up smaller single/differential signals to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
  4-Digit 7-segment LED Display: A 4-digit 7-segments LED display PCB module driven by a TM1637 control IC via 1-wire protocol.
  Mcp23017 Interface Module: The MCP23017 is capable of converting 16-bit parallel data to serial data of the IIC interface and converting each other. An internal integrated power-on reset (POR) circuit is reset to the device's default state. The two opposites become the interrupt source output. The polarity toggle register configures the GPIO input polarity.
  Niren can bus module: Niren can bus module availabe on ebay and others. Pcb view assumes that you unsolder the 7 pin header and resolder it on the bottom of the module to connect to the pcb. The two jumpers and the can bus connector remain on the top of the board and don't appear in pcb view.
